# Fritzing sketch Client (saved by Fritzing 0.9.3b)
breadboards: 1

parts:
  U1 = ESP32S-HiLetgo [part_number=ESP32S-HiLetgo]
  M1 = Stepper Motor - Bipolar
  A1 = DM860A Stepper Motor Driver
  M2 = 1 chan 5v relay module
  S1 = D2F-FL Omron Snap Action Limit Switch with Level
  S2 = Reed switch [package=THT]
  PS1 = prefix0000 [part_number=S-350-60]
  M3 = RioRand LM2596
  A2 = RGB Strip LED

nets:
  N1: U1.GPIO39, S2.pin_1
  N2: U1.GPIO32, A1.DIR+(+5V)
  N3: U1.GPIO33, A1.PUL+(+5V)
  N4: U1.GND, A1.ENBL-(ENB), A1.DIR-(DIR), A1.PUL-(PUL), M2.pin_2, S1.Pin_1, S2.pin_2, M3.Pin_4
  N5: U1.GPIO13, M2.pin_3
  N6: U1.VIN, M2.pin_1, M3.Pin_3
  N7: U1.GPIO5, S1.Pin_2
  N8: U1.GPIO18, A1.ENBL+(+5V)
  N9: M1.A, A1.B+
  N10: M1.C, A1.B-
  N11: M1.B, A1.A+
  N12: M1.D, A1.A-
  N13: A1.VDC, M2.pin_4, PS1.connector1, M3.Pin_1
  N14: A1.GND, PS1.connector4, M3.Pin_2, A2.Green_Connect
  N15: M2.pin_5, A2.Common_Connect

custom parts:
  ESP32S-HiLetgo: HiLetgo ESP-WROOM-32 ESP32 ESP-32S Development Board 2.4GHz Dual-Mode WiFi + Bluetooth Dual Cores Microcontroller The ESP32 integrated with Antenna switches, RF Balun, power amplifiers, low-noise amplifiers, filters, and management modules, and the entire solution occupies the least area of PCB. 2.4 GHz Wi-Fi plus Bluetooth dual-mode chip, with TSMC Ultra-low power consumption 40nm technology,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
  DM860A Stepper Motor Driver: DM860A is a type of two-phase hybrid stepping motor driver, The drive voltage of which is from 24VDC to 80VDC. It is designed for use with 2-phase hybrid stepper motor of all kinds with 57mm to 110mm outside diameter and less than 8.0A phase current. Mar 2023: Correct pcb layerId as the part won't save correctly in a .fzz file as is.
  1 chan 5v relay module: 1 Channel 5V Relay Module Board Shield with Optocoupler Support High and Low Level Trigger for Arduino.
  D2F-FL Omron Snap Action Limit Switch with Level: Snap action switch with stainless steel lever.
  RGB Strip LED: A tri-color Strip LED with red, green and blue. Pin order: red - common cathode - blue - green
