# Fritzing sketch Host (saved by Fritzing 0.9.3b)
breadboards: 1

parts:
  U1 = ESP32S-HiLetgo [part_number=ESP32S-HiLetgo]
  Part1 = sensor_biometrico
  LCD2004-I2C1 = LCD2004-I2C
  S1 = Pushbutton [package="[THT]"]
  C1 = Electrolytic Capacitor [package="2cm H-Type"]
  J1 = Piezo Speaker
  M1 = AC-05-03

nets:
  N1: U1.3.3, Part1.VCC
  GND: U1.GND, Part1.GND, LCD2004-I2C1.GND, S1.Pin_3, S1.Pin_4, C1.-, J1.pin1, M1.pin_4
  VIN: U1.VIN, LCD2004-I2C1.VCC, C1.+, M1.pin_3
  N2: U1.GPIO16, Part1.TX
  N3: U1.GPIO17, Part1.RX
  N4: U1.GPIO5, J1.pin2
  N5: U1.GPIO21, LCD2004-I2C1.SDA
  N6: U1.GPIO22, LCD2004-I2C1.SCL
  N7: S1.Pin_1, S1.Pin_2

custom parts:
  ESP32S-HiLetgo: HiLetgo ESP-WROOM-32 ESP32 ESP-32S Development Board 2.4GHz Dual-Mode WiFi + Bluetooth Dual Cores Microcontroller The ESP32 integrated with Antenna switches, RF Balun, power amplifiers, low-noise amplifiers, filters, and management modules, and the entire solution occupies the least area of PCB. 2.4 GHz Wi-Fi plus Bluetooth dual-mode chip, with TSMC Ultra-low power consumption 40nm technology,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
  sensor_biometrico: Adafruit Optical Fingerprint Sensor
  LCD2004-I2C: A standard character display with 4x20 characters. Comes in many colors with LCM2004 IIC attached.
  AC-05-03: AC-DC 220V to 5V Step-Down Power Supply Module
